// Logisim project projeto de circuito 2.circ as structural Verilog: 15 circuits, main circuit main
module main (
  input  SelecionaXouY,
  input  SelecionaAouB,
  input  in_3,
  input  in_4,
  input  in_5,
  input  in_6,
  input  in_7,
  input  in_8,
  input  in_9,
  input  in_10,
  input  in_11,
  input  in_12
);

  wire Clock_out, numerouser_1_out_7, numerouseroeste_1_out_7, Seletor_out_5, Seletor_out_7;
  wire [3:0] \Memoria4bits_saída , numerouser_1_out_6, numerouseroeste_1_out_6, Seletor_out_6, Seletor_out_8;
  wire [4:0] numerouser_1_s, numerouseroeste_1_s;

  LED led_1 (.in(numerouser_1_out_7));
  Hex_Digit_Display hex_digit_display_1 (.value(numerouser_1_out_6));  // open: dp
  NumeroUser numerouser_1 (
    .out_7(numerouser_1_out_7), .out_6(numerouser_1_out_6), .in_1(in_3), .in_2(in_4), .in_3(in_5),
    .in_4(in_6), .in_5(in_7), .S(numerouser_1_s));
  LED led_2 (.in(Seletor_out_5));
  Clock Clock (.out(Clock_out));
  Hex_Digit_Display hex_digit_display_2 (.value(\Memoria4bits_saída ));  // open: dp
  MemoriaNumeroUser Memoria4bits (.Entrada(Seletor_out_6), .Clock(Clock_out), .\Saída (\Memoria4bits_saída ));
  LED led_3 (.in(Seletor_out_7));
  Hex_Digit_Display hex_digit_display_3 (.value(Seletor_out_8));  // open: dp
  Seletor Seletor (
    .in_1(SelecionaXouY), .in_2(SelecionaAouB), .in_3(numerouser_1_s), .in_4(numerouseroeste_1_s),
    .out_6(Seletor_out_6), .out_8(Seletor_out_8), .out_5(Seletor_out_5), .out_7(Seletor_out_7));
  LED led_4 (.in(numerouseroeste_1_out_7));
  Hex_Digit_Display hex_digit_display_4 (.value(numerouseroeste_1_out_6));  // open: dp
  NumeroUserOeste numerouseroeste_1 (
    .S(numerouseroeste_1_s), .out_7(numerouseroeste_1_out_7), .out_6(numerouseroeste_1_out_6), .in_1(in_8),
    .in_2(in_9), .in_3(in_10), .in_4(in_11), .in_5(in_12));

  // Notes on the sheet:
  //   Jogador A
  //   X
  //   Y
  //   Jogador B
endmodule

module NumeroUser (
  input  in_1,
  input  in_2,
  input  in_3,
  input  in_4,
  input  in_5,
  output [3:0] out_6,
  output out_7,
  output [4:0] S
);


  assign out_6 = {in_2, in_3, in_4, in_5};
  assign out_7 = in_1;
  assign S = {in_1, in_2, in_3, in_4, in_5};
endmodule

// NumeroUser
module NumeroUserOeste (
  input  in_1,
  input  in_2,
  input  in_3,
  input  in_4,
  input  in_5,
  output [3:0] out_6,
  output out_7,
  output [4:0] S
);


  assign out_6 = {in_2, in_3, in_4, in_5};
  assign out_7 = in_1;
  assign S = {in_1, in_2, in_3, in_4, in_5};
endmodule

module Seletor (
  input  in_1,
  input  in_2,
  input  [4:0] in_3,
  input  [4:0] in_4,
  output out_5,
  output [3:0] out_6,
  output out_7,
  output [3:0] out_8
);

  wire [4:0] demultiplexer_1_out0, demultiplexer_1_out1, multiplexer_1_out;

  converte5para4 converte5para4_1 (.out_3(out_5), .in_1(demultiplexer_1_out0), .out_2(out_6));
  Demultiplexer #(.width(5), .enable("false")) demultiplexer_1 (
    .out0(demultiplexer_1_out0), .out1(demultiplexer_1_out1), .in(multiplexer_1_out), .sel(in_1));
  Multiplexer #(.width(5), .enable("false")) multiplexer_1 (
    .in0(in_3), .in1(in_4), .out(multiplexer_1_out), .sel(in_2));
  converte5para4 converte5para4_2 (.out_3(out_7), .in_1(demultiplexer_1_out1), .out_2(out_8));
endmodule

module MemoriaNumeroUser (
  input  Clock,
  input  [3:0] Entrada,
  output [3:0] \Saída 
);

  D_Flip_Flop d_ff_1 (.clk(Clock), .D(Entrada[0]), .Q(\Saída [0]));  // open: Qn, preset, en, reset
  D_Flip_Flop d_ff_2 (.clk(Clock), .D(Entrada[1]), .Q(\Saída [1]));  // open: Qn, preset, en, reset
  D_Flip_Flop d_ff_3 (.clk(Clock), .D(Entrada[2]), .Q(\Saída [2]));  // open: Qn, preset, en, reset
  D_Flip_Flop d_ff_4 (.clk(Clock), .D(Entrada[3]), .Q(\Saída [3]));  // open: Qn, preset, en, reset
endmodule

module RandomNumber (
  input  Clock,
  input  Reset,
  output [4:0] out_3,
  output [4:0] out_4
);

  wire converte5para4_1_out_3, converte5para4_2_out_3;
  wire [3:0] converte5para4_1_out_2, converte5para4_2_out_2;

  LED led_1 (.in(converte5para4_2_out_3));
  LED led_2 (.in(converte5para4_1_out_3));
  Hex_Digit_Display hex_digit_display_1 (.value(converte5para4_1_out_2));  // open: dp
  converte5para4 converte5para4_1 (.out_3(converte5para4_1_out_3), .in_1(out_3), .out_2(converte5para4_1_out_2));
  Random #(.width(5)) random_1 (.clk(Clock), .out(out_3), .clr(Reset));  // open: next
  Random #(.width(5)) random_2 (.clk(Clock), .out(out_4), .clr(Reset));  // open: next
  converte5para4 converte5para4_2 (.out_3(converte5para4_2_out_3), .in_1(out_4), .out_2(converte5para4_2_out_2));
  Hex_Digit_Display hex_digit_display_2 (.value(converte5para4_2_out_2));  // open: dp
endmodule

module converte5para4 (
  input  [4:0] in_1,
  output [3:0] out_2,
  output out_3
);


  assign out_2 = in_1[3:0];
  assign out_3 = in_1[4];
endmodule

module analisador (
  input  [4:0] X_random,
  input  [4:0] Y_random,
  input  [4:0] X_user,
  input  [4:0] Y_user,
  output Acertou,
  output Igual,
  output Maior,
  output Menor
);

  wire comparadordeigualdade_1_igual, comparadordeigualdade_2_igual;
  wire [5:0] somador_2_out_3, Somador_out_3;

  Somador Somador (.X(X_random), .Y(Y_random), .out_3(Somador_out_3));
  comparadorDeIgualdade comparadordeigualdade_1 (.A(X_random), .B(X_user), .Igual(comparadordeigualdade_1_igual));
  Somador somador_2 (.X(X_user), .Y(Y_user), .out_3(somador_2_out_3));
  and and_1 (Acertou, comparadordeigualdade_1_igual, comparadordeigualdade_2_igual, Igual);
  comparador comparador_1 (.A(Somador_out_3), .B(somador_2_out_3), .Igual(Igual), .Maior(Maior), .Menor(Menor));
  comparadorDeIgualdade comparadordeigualdade_2 (.A(Y_random), .B(Y_user), .Igual(comparadordeigualdade_2_igual));
endmodule

module Somador (
  input  [4:0] X,
  input  [4:0] Y,
  output [5:0] out_3
);

  wire [1:0] Converte5_para_4_1_out_3;
  wire [3:0] adder_1_out, adder_2_out, adder_3_out, adder_4_out, Converte5_para_4_1_2_out_2,
       Converte5_para_4_1_out_2, multiplexer_1_out, multiplexer_2_out, negator_1_out, negator_2_out,
       negator_3_out, negator_4_out;
  wire [4:4] adder_1_cout, adder_4_cout;
  wire [5:5] comparator_1_lt, not_1_out;

  converte5para4 Converte5_para_4_1 (.out_3(Converte5_para_4_1_out_3[0]), .in_1(X), .out_2(Converte5_para_4_1_out_2));
  converte5para4 Converte5_para_4_1_2 (
    .out_3(Converte5_para_4_1_out_3[1]), .in_1(Y), .out_2(Converte5_para_4_1_2_out_2));
  Negator #(.width(4)) negator_1 (.in(Converte5_para_4_1_out_2), .out(negator_1_out));
  Negator #(.width(4)) negator_2 (.in(Converte5_para_4_1_2_out_2), .out(negator_2_out));
  Adder #(.width(4)) adder_1 (
    .a(Converte5_para_4_1_out_2), .b(Converte5_para_4_1_2_out_2), .out(adder_1_out), .cout(adder_1_cout[4]));  // open: cin
  Adder #(.width(4)) adder_2 (.a(negator_1_out), .b(Converte5_para_4_1_2_out_2), .out(adder_2_out));  // open: cin, cout
  Comparator #(.width(4)) comparator_1 (
    .a(Converte5_para_4_1_out_2), .b(Converte5_para_4_1_2_out_2), .lt(comparator_1_lt[5]));  // open: gt, eq
  not not_1 (not_1_out[5], comparator_1_lt[5]);
  Adder #(.width(4)) adder_3 (.a(Converte5_para_4_1_out_2), .b(negator_2_out), .out(adder_3_out));  // open: cin, cout
  Adder #(.width(4)) adder_4 (
    .a(Converte5_para_4_1_out_2), .b(Converte5_para_4_1_2_out_2), .out(adder_4_out), .cout(adder_4_cout[4]));  // open: cin
  Multiplexer #(.width(4), .enable("false")) multiplexer_1 (
    .in0(adder_2_out), .in1(negator_3_out), .out(multiplexer_1_out), .sel(comparator_1_lt[5]));
  Negator #(.width(4)) negator_3 (.in(adder_2_out), .out(negator_3_out));
  Multiplexer #(.width(4), .enable("false")) multiplexer_2 (
    .in0(adder_3_out), .in1(negator_4_out), .out(multiplexer_2_out), .sel(not_1_out[5]));
  Negator #(.width(4)) negator_4 (.in(adder_3_out), .out(negator_4_out));
  Multiplexer #(.select(2), .width(6), .enable("false")) multiplexer_3 (
    .in0({1'b0, adder_1_cout[4], adder_1_out}), .in1({comparator_1_lt[5], 1'b0, multiplexer_1_out}),
    .in2({not_1_out[5], 1'b0, multiplexer_2_out}), .in3({1'b1, adder_4_cout[4], adder_4_out}), .out(out_3),
    .sel(Converte5_para_4_1_out_3));
endmodule

module comparador (
  input  [5:0] A,
  input  [5:0] B,
  output Igual,
  output Maior,
  output Menor
);

  wire and_1_out, and_2_out, and_3_out, and_4_out, and_5_out, and_6_out, and_7_out, and_8_out, and_9_out,
       and_10_out, comparator_1_eq, comparator_1_lt, or_1_out;

  and and_1 (and_1_out, ~1'b0, ~A[0], ~A[1], ~A[2], ~A[3], ~A[4]);  // AND_Gate
  Comparator #(.width(5)) comparator_1 (
    .a(A[4:0]), .b(B[4:0]), .eq(comparator_1_eq), .lt(comparator_1_lt));  // open: gt
  and and_2 (and_2_out, ~1'b0, ~B[0], ~B[1], ~B[2], ~B[3], ~B[4]);  // AND_Gate
  and and_3 (and_3_out, and_1_out, and_2_out);
  and and_4 (and_4_out, A[5], B[5]);
  or or_1 (or_1_out, and_4_out, and_5_out);
  and and_5 (and_5_out, ~A[5], ~B[5]);  // AND_Gate
  and and_6 (and_6_out, comparator_1_eq, or_1_out);
  or or_2 (Igual, and_3_out, and_6_out);
  and and_7 (and_7_out, ~A[5], ~1'b0);  // AND_Gate
  and and_8 (and_8_out, B[5], 1'b1);
  and and_9 (and_9_out, comparator_1_lt, or_1_out);
  and and_10 (and_10_out, and_7_out, ~Igual, and_8_out);  // AND_Gate
  or or_3 (Maior, and_9_out, and_10_out);
  and and_11 (Menor, ~Igual, ~Maior);  // AND_Gate

  // Notes on the sheet:
  //   Verifica se os sinais são iguais
  //   Verifica se os números são zeros
endmodule

module comparadorDeIgualdade (
  input  [4:0] A,
  input  [4:0] B,
  output Igual
);

  wire and_1_out, and_2_out, and_3_out, and_4_out, igual_1_s, igual_2_s, igual_3_s, igual_4_s, igual_5_s;

  and and_1 (and_1_out, ~1'b0, ~A[0], ~A[1], ~A[2], ~A[3]);  // AND_Gate
  Igual igual_1 (.A(A[0]), .B(B[0]), .S(igual_1_s));
  Igual igual_2 (.A(A[1]), .B(B[1]), .S(igual_2_s));
  and and_2 (and_2_out, ~1'b0, ~B[0], ~B[1], ~B[2], ~B[3]);  // AND_Gate
  Igual igual_3 (.A(A[2]), .B(B[2]), .S(igual_3_s));
  Igual igual_4 (.A(A[3]), .B(B[3]), .S(igual_4_s));
  Igual igual_5 (.A(A[4]), .B(B[4]), .S(igual_5_s));
  and and_3 (and_3_out, igual_1_s, igual_2_s, igual_3_s, igual_4_s, igual_5_s);
  and and_4 (and_4_out, and_1_out, and_2_out);
  or or_1 (Igual, and_4_out, and_3_out);
endmodule

module Igual (
  input  A,
  input  B,
  output S
);

  wire and_1_out, and_2_out;

  and and_1 (and_1_out, A, B);
  and and_2 (and_2_out, ~A, ~B);  // AND_Gate
  or or_1 (S, and_1_out, and_2_out);
endmodule

module Flip_Flop_D_subida (
  input  D,
  output Q,
  output nQ
);

  wire CLK_out, nand_1_out, nand_2_out;

  Clock CLK (.out(CLK_out));
  nand nand_1 (nand_1_out, D, CLK_out);
  nand nand_2 (nand_2_out, CLK_out, ~D);  // NAND_Gate
  nand nand_3 (Q, nand_1_out, nQ);
  nand nand_4 (nQ, Q, nand_2_out);

  // Notes on the sheet:
  //   O flip flop tipo D serve para guardar um valor.
endmodule

module \Circuito_de_9_à_0  (
  input  Q3,
  input  Q2,
  input  Q1,
  input  Q0,
  output S3,
  output S2,
  output S1,
  output S0
);

  wire and_1_out, and_2_out, and_3_out, and_4_out, and_5_out, and_6_out, and_7_out, and_8_out, and_9_out,
       not_1_out, not_2_out, not_3_out, not_4_out, not_5_out, not_6_out, not_7_out, not_8_out, not_9_out,
       not_10_out;

  not not_1 (not_1_out, Q3);
  not not_2 (not_2_out, Q2);
  not not_3 (not_3_out, Q1);
  not not_4 (not_4_out, Q0);
  not not_5 (not_5_out, Q1);
  not not_6 (not_6_out, Q0);
  not not_7 (not_7_out, Q1);
  not not_8 (not_8_out, Q0);
  not not_9 (not_9_out, Q1);
  not not_10 (not_10_out, Q0);
  not not_11 (S0, Q0);
  and and_1 (and_1_out, not_1_out, not_2_out, not_3_out, not_4_out);
  and and_2 (and_2_out, Q3, Q0);
  and and_3 (and_3_out, Q3, Q1);
  and and_4 (and_4_out, Q2, Q0);
  and and_5 (and_5_out, Q2, Q1);
  and and_6 (and_6_out, Q3, not_5_out, not_6_out);
  and and_7 (and_7_out, Q1, Q0);
  and and_8 (and_8_out, Q2, not_7_out, not_8_out);
  and and_9 (and_9_out, Q3, not_9_out, not_10_out);
  or or_1 (S3, and_1_out, and_2_out, and_3_out);
  or or_2 (S2, and_4_out, and_5_out, and_6_out);
  or or_3 (S1, and_7_out, and_8_out, and_9_out);

  // Notes on the sheet:
  //   Circuito para usar no contador de 0 à 9
endmodule

module \Contador_de_9_à_0  (
  input  CLOCK,
  input  CLEAR,
  input  ENABLE,
  output [3:0] out_4,
  output [3:0] out_5
);

  wire \Circuito_9_à_0_s0 , \Circuito_9_à_0_s1 , \Circuito_9_à_0_s2 , \Circuito_9_à_0_s3 ;

  D_Flip_Flop d_ff_1 (
    .clk(CLOCK), .D(\Circuito_9_à_0_s3 ), .Q(out_4[3]), .Qn(out_5[3]), .en(ENABLE), .reset(CLEAR));  // open: preset
  D_Flip_Flop d_ff_2 (
    .clk(CLOCK), .D(\Circuito_9_à_0_s2 ), .Q(out_4[2]), .Qn(out_5[2]), .en(ENABLE), .reset(CLEAR));  // open: preset
  D_Flip_Flop d_ff_3 (
    .clk(CLOCK), .D(\Circuito_9_à_0_s1 ), .Q(out_4[1]), .Qn(out_5[1]), .en(ENABLE), .reset(CLEAR));  // open: preset
  \Circuito_de_9_à_0  \Circuito_9_à_0  (
    .Q3(out_4[3]), .Q2(out_4[2]), .Q1(out_4[1]), .Q0(out_4[0]), .S3(\Circuito_9_à_0_s3 ),
    .S2(\Circuito_9_à_0_s2 ), .S1(\Circuito_9_à_0_s1 ), .S0(\Circuito_9_à_0_s0 ));
  D_Flip_Flop d_ff_4 (
    .clk(CLOCK), .D(\Circuito_9_à_0_s0 ), .Q(out_4[0]), .Qn(out_5[0]), .en(ENABLE), .reset(CLEAR));  // open: preset
  Hex_Digit_Display hex_digit_display_1 (.value(out_4));  // open: dp
endmodule
